# Fritzing sketch BasicStrip (saved by Fritzing 0.9.2b)
breadboards: 1

parts:
  R1 = Resistor [tolerance=±5% resistance=220 package=THT]
  R2 = Resistor [tolerance=±5% resistance=220 package=THT]
  Part1 = Arduino Uno (Rev3)
  C1 = Electrolytic Capacitor [capacitance=1mF voltage=6.3V package="100 mil [THT, electrolytic]"]
  Part3 = NeoPixel Stick [part_number=1426]

nets:
  N1: R1.Pin_0, Part1.D6_PWM
  N2: R1.Pin_1, R2.Pin_0
  N3: R2.Pin_1, Part3.DATAIN
  5V: Part1.5V, C1.+, Part3.+5V
  GND: Part1.GND, C1.-, Part3.GND

notes:
  You want to have 300-500 Ohms of resistance between the Arduino and the "Data In" connection for the NeoPixel. (In this case, I'm showing 2 220 Ohm resistors being used, but however you can get there....)
  You also want to have a 1000 micro-Farad capacitor spanning the +5V and ground lines, so that there is something to help buffer sudden changes in the current (e.g., when power suddenly comes on, and may be fluctuating outside of designed ranges). This is arguably less of an issue when you're powering directly off the Arduino, vs. plugging into an external supply or battery, but it's a good habit to follow.

custom parts:
  NeoPixel Stick: Make your own little LED strip arrangement with this stick of NeoPixel LEDs. We crammed 8 of the tiny 5050 (5mm x 5mm) smart RGB LEDs onto a PCB with mounting holes and a chainable design. Use only one microcontroller pin to control as many as you can chain together! Each LED is addressable as the driver chip is inside the LED. Each one has ~18mA constant current drive so the color will be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
