# Fritzing sketch Logic Translator Demo (saved by Fritzing 0.9.2b)
breadboards: 1

parts:
  Part1 = Bi-Directional Logic Level Converter [part_number=BOB-12009]
  Part2 = Arduino Mega 2560 (Rev3)
  Part3 = Arduino Uno (Rev3)

nets:
  N1: Part1.LV, Part3.3V3
  N2: Part1.GND#3, Part3.GND
  N3: Part1.LV3, Part3.D1/TX
  N4: Part1.LV4, Part3.D0/RX
  N5: Part1.HV4, Part2.D18/TX1
  N6: Part1.HV3, Part2.D19/RX1
  N7: Part1.GND#8, Part2.GND
  N8: Part1.HV, Part2.5V

notes:
  Arduino Mega represents the 5V side of the communications link (e.g., an Arduino controlling lights, etc., on the robot).
  Arduino Uno represents the 3.3V side of the link (e.g., the RoboRio, either directly connected or plumbed through the UART on the NavX board).

custom parts:
  Bi-Directional Logic Level Converter: Description: If you've ever tried to connect a 3.3V device to a 5V system, you know what a challenge it can be. The SparkFun bi-directional logic level converter is a small device that safely steps down 5V signals to 3.3V AND steps up 3.3V to 5V at the same time. This level converter also works with 2.8V and 1.8V devices. What really separates this Logic level converter from our previous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
