# Fritzing sketch LED lighting prototype (saved by Fritzing 0.9.3b)
breadboards: 1

parts:
  Part1 = Arduino Uno (Rev3)
  R1 = Resistor [tolerance=±5% resistance=220 package=THT]
  C1 = Electrolytic Capacitor [capacitance=1µF package="100 mil [THT, electrolytic]"]
  R2 = Resistor [tolerance=±5% resistance=220 package=THT]
  VCC1 = Battery
  NEOPIXEL1 = Neopixel Strip -- White (30/m)

nets:
  N1: Part1.D6_PWM, R1.Pin_0
  GND: Part1.GND, C1.-, VCC1.-, NEOPIXEL1.GND
  N2: R1.Pin_1, R2.Pin_0
  N3: C1.+, VCC1.+, NEOPIXEL1.+5V
  N4: R2.Pin_1, NEOPIXEL1.Din

custom parts:
  Neopixel Strip -- White (30/m): These NeoPixel strips have 30 digitally-addressable pixel LEDs per meter and are very affordable and are only 12.5 mm wide, 10 mm if you remove the strip from the casing.
