# Fritzing sketch Sally continuous lighting (saved by Fritzing 0.9.3b)
breadboards: 1

parts:
  cntl1 = roboRIO
  Mod1 = VRM
  Mod2 = VRM
  NEOPIXEL1 = Neopixel Strip -- White (30/m) [part_number=1376]
  NEOPIXEL2 = Neopixel Strip -- White (30/m) [part_number=1376]
  R1 = Resistor [tolerance=±5% resistance=220 package=THT]
  C3 = Electrolytic Capacitor [capacitance=1000μF package="1010 [SMD, electrolytic]"]
  C4 = Electrolytic Capacitor [capacitance=1000μF package="1010 [SMD, electrolytic]"]

nets:
  N1: cntl1.Power_GND, cntl1.Pin_6, cntl1.IN_A1_GND, cntl1.PWM0_GND, Mod2.5V_2A_GND0, Mod2.12V_500mA_GND0, NEOPIXEL1.GND, C3.-
  N2: cntl1.PWM0_SIG, R1.Pin_0
  N3: Mod1.5V_2A_GND0, Mod1.12V_2A_GND0, NEOPIXEL2.GND, C4.-
  N4: Mod1.5V_2A_5V0, NEOPIXEL2.+5V, C4.+
  N5: Mod2.5V_2A_5V0, NEOPIXEL1.+5V, C3.+
  N6: NEOPIXEL1.Din, R1.Pin_1
  N7: NEOPIXEL1.Dout, NEOPIXEL2.Din

custom parts:
  Neopixel Strip -- White (30/m): These NeoPixel strips have 30 digitally-addressable pixel LEDs per meter and are very affordable and are only 12.5 mm wide, 10 mm if you remove the strip from the casing.
