# Fritzing sketch Sally lighting (saved by Fritzing 0.9.3b)
breadboards: 1

parts:
  cntl1 = roboRIO
  Mod1 = VRM
  Mod2 = VRM
  NEOPIXEL1 = Neopixel Strip -- White (30/m) [part_number=1376]
  NEOPIXEL2 = Neopixel Strip -- White (30/m) [part_number=1376]
  R1 = Resistor [tolerance=±5% resistance=330 package=THT]
  C1 = Electrolytic Capacitor [capacitance=1000μF package="1010 [SMD, electrolytic]"]
  C2 = Electrolytic Capacitor [capacitance=1000μF package="1010 [SMD, electrolytic]"]

nets:
  GND: cntl1.Power_GND, cntl1.Pin_28, cntl1.Pin_6, cntl1.SPI_GND, cntl1.RY0_GND, cntl1.PWM0_GND, Mod1.5V_2A_GND0, Mod1.12V_2A_GND0, Mod2.5V_2A_GND0, Mod2.12V_500mA_GND0, NEOPIXEL1.GND, NEOPIXEL2.GND, C1.-, C2.-
  N1: cntl1.PWM0_SIG, R1.Pin_0
  N2: Mod1.5V_2A_5V0, NEOPIXEL2.+5V, C2.+
  N3: Mod2.5V_2A_5V0, NEOPIXEL1.+5V, C1.+
  N4: NEOPIXEL1.Din, NEOPIXEL2.Din, R1.Pin_1

custom parts:
  Neopixel Strip -- White (30/m): These NeoPixel strips have 30 digitally-addressable pixel LEDs per meter and are very affordable and are only 12.5 mm wide, 10 mm if you remove the strip from the casing.
